# Fritzing sketch rgb-ethernet (saved by Fritzing 0.8.5b)
circuit board: 5.42637cm x 5.39594cm
breadboards: 1

parts:
  R1 = Resistor [tolerance=±5% resistance=560 package=THT]
  R2 = Resistor [tolerance=±5% resistance=560 package=THT]
  R3 = Resistor [tolerance=±5% resistance=560 package=THT]
  LED1 = LED - 5mm [color="Blue (525nm)" package="5 mm [THT]"]
  LED2 = LED - 5mm [color="Green (570nm)" package="5 mm [THT]"]
  LED3 = LED - 5mm [color="Red (635nm)" package="5 mm [THT]"]
  Arduino_Ethernet_Shield1 = Arduino Ethernet Shield (Rev3)

nets:
  N1: R1.Pin_0, LED1.anode
  N2: R1.Pin_1, Arduino_Ethernet_Shield1.D2
  N3: R2.Pin_0, LED2.anode
  N4: R2.Pin_1, Arduino_Ethernet_Shield1.PWM_D3
  N5: R3.Pin_0, LED3.anode
  N6: R3.Pin_1, Arduino_Ethernet_Shield1.SDCS
  N7: LED1.cathode, LED2.cathode, LED3.cathode, Arduino_Ethernet_Shield1.GND
